// Digital circuit fetch.dig as structural Verilog
module fetch (
  input  C,
  output error,
  output [15:0] instr_o
);

  wire C_t, decoder_1_out_0, ovf;
  wire [5:0] PC_out;
  wire [15:0] ramdualport_1_d;

  Decoder decoder_1 (.sel(ovf), .out_0(decoder_1_out_0), .out_1(error));
  Counter #(.Bits(6)) PC (.en(1'b1), .C(C_t), .clr(1'b0), .out(PC_out), .ovf(ovf));
  and and_1 (C_t, C, decoder_1_out_0);
  RAMDualPort #(.AddrBits(6), .isProgramMemory("true"), .Bits(16)) ramdualport_1 (
    .A(PC_out), .Din({16{1'b0}}), .str(1'b0), .C(C_t), .ld(1'b1), .D(ramdualport_1_d));
  Register #(.Bits(16)) IR (.D(ramdualport_1_d), .C(C_t), .en(1'b1), .Q(instr_o));
endmodule
